# Fritzing sketch Wireless_LED_Controller (saved by Fritzing 0.9.3b)

parts:
  U1 = NodeMCU V1.0
  LED2 = LEDs [package=led10mm]
  LED3 = RGB LED (com. cathode, rbg) [package="5 mm [THT]"]

nets:
  N1: U1.D4, LED2.A
  N2: U1.GND, LED2.C, LED3.common_cathode
  N3: U1.D5, LED3.red_anode
  N4: U1.D6, LED3.green_anode
  N5: U1.D7, LED3.blue_anode

custom parts:
  NodeMCU V1.0: ESP8266 based NodeMCU
